# Fritzing sketch Plan B - Schema (saved by Fritzing 1.0.1rc)
breadboards: 2

parts:
  M1 = DC Motor [voltage_(max)=12V voltage_(min)=3V]
  M2 = DC Motor [voltage_(max)=12V voltage_(min)=3V]
  B1 = Pololu QTR-8 Reflectabce Sensor array [package=THT]
  R1 = Resistor [tolerance=±5% power=0.25W resistance=220 package=THT]
  R7 = Resistor [tolerance=±5% power=0.25W resistance=220 package=THT]
  ESP32-WROOM_DEVKIT2 = MH-ET LIVE ESP32 DEVKIT 38 pins
  LED1 = smd LED [color="White (4500K)" package="0805 [SMD]"]
  LED7 = smd LED [color="Orange (612nm)" package="0805 [SMD]"]
  LED2 = smd LED [color="White (4500K)" package="0805 [SMD]"]
  LED5 = smd LED [color="Orange (612nm)" package="0805 [SMD]"]
  DRV8833 = Adafruit DRV8833 DC/Stepper Motor Driver [part_number="Adafruit #3297"]
  R5 = Resistor [tolerance=±5% power=0.25W resistance=220 package=THT]
  R2 = Resistor [tolerance=±5% power=0.25W resistance=220 package=THT]
  LED4 = smd LED [color="Red (635nm)" package="0805 [SMD]"]
  LED8 = smd LED [color="Orange (612nm)" package="0805 [SMD]"]
  LED6 = smd LED [color="Red (635nm)" package="0805 [SMD]"]
  LED3 = smd LED [color="Orange (612nm)" package="0805 [SMD]"]
  R8 = Resistor [tolerance=±5% power=0.25W resistance=220 package=THT]
  R4 = Resistor [tolerance=±5% power=0.25W resistance=220 package=THT]
  R3 = Resistor [tolerance=±5% power=0.25W resistance=220 package=THT]
  R6 = Resistor [tolerance=±5% power=0.25W resistance=220 package=THT]
  L7805CV = Voltage Regulator [package=to220-adj]
  VCC_8_4V = Battery
  S1_(Start/Stop) = Pushbutton [package="[THT]"]

nets:
  N1: M1.pin_1, DRV8833.AOUT2
  N2: M1.pin_2, DRV8833.AOUT1
  N3: M2.pin_1, DRV8833.BOUT1
  N4: M2.pin_2, DRV8833.BOUT2
  N5: B1.pin1, B1.pin15, R1.Pin_1, R7.Pin_1, ESP32-WROOM_DEVKIT2.GND#64
  N6: B1.pin6, ESP32-WROOM_DEVKIT2.SVP
  N7: B1.pin7, ESP32-WROOM_DEVKIT2.SVN
  N8: B1.pin8, ESP32-WROOM_DEVKIT2.IO34
  N9: B1.pin9, ESP32-WROOM_DEVKIT2.IO35
  N10: B1.pin10, ESP32-WROOM_DEVKIT2.IO32
  N11: B1.pin11, ESP32-WROOM_DEVKIT2.IO33
  N12: B1.pin14, ESP32-WROOM_DEVKIT2.3V3
  N13: R1.Pin_0, LED1.cathode
  N14: R7.Pin_0, LED7.cathode
  N15: ESP32-WROOM_DEVKIT2.IO25, LED2.anode
  N16: ESP32-WROOM_DEVKIT2.IO26, LED5.anode
  N17: ESP32-WROOM_DEVKIT2.IO27, LED4.anode
  N18: ESP32-WROOM_DEVKIT2.IO14, LED8.anode
  N19: ESP32-WROOM_DEVKIT2.GND#58, DRV8833.GND, R5.Pin_1, R2.Pin_1, R8.Pin_1, R4.Pin_1, L7805CV.IN, VCC_8_4V.-
  N20: ESP32-WROOM_DEVKIT2.5V, DRV8833.PWRIN, L7805CV.OUT
  N21: ESP32-WROOM_DEVKIT2.IO23, LED7.anode
  N22: ESP32-WROOM_DEVKIT2.IO22, LED1.anode
  N23: ESP32-WROOM_DEVKIT2.IO21, LED6.anode
  N24: ESP32-WROOM_DEVKIT2.GND#70, R3.Pin_1, R6.Pin_1, S1_(Start/Stop).Pin_3, S1_(Start/Stop).Pin_4
  N25: ESP32-WROOM_DEVKIT2.IO19, DRV8833.BIN1
  N26: ESP32-WROOM_DEVKIT2.IO18, DRV8833.BIN2
  N27: ESP32-WROOM_DEVKIT2.IO17, DRV8833.AIN1
  N28: ESP32-WROOM_DEVKIT2.IO16, DRV8833.AIN2
  N29: ESP32-WROOM_DEVKIT2.IO2, S1_(Start/Stop).Pin_1, S1_(Start/Stop).Pin_2
  N30: ESP32-WROOM_DEVKIT2.IO15, LED3.anode
  N31: LED2.cathode, R2.Pin_0
  N32: LED5.cathode, R5.Pin_0
  N33: DRV8833.VMOTOR, L7805CV.ADJ, VCC_8_4V.+
  N34: LED4.cathode, R4.Pin_0
  N35: LED8.cathode, R8.Pin_0
  N36: LED6.cathode, R6.Pin_0
  N37: LED3.cathode, R3.Pin_0

notes:
  Designed by:
  Louis Van Roosmaelen

custom parts:
  MH-ET LIVE ESP32 DEVKIT 38 pins: http://mh.nodebb.com/topic/2/mh-et-live-esp32-devkit
  Adafruit DRV8833 DC/Stepper Motor Driver: Spin two DC motors or step one bi-polar or uni-polar stepper with up to 1.2A per channel using the DRV8833. This motor driver chip is a nice alternative to the TB6612 driver. Like that chip, you get 2 full H-bridges, but this chip is better for low voltage uses (can run from 2.7V up to 10.8V motor power) and has built in current limiting capability. We set it up for 1A current limiting so you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
  Battery: Your standard 2x 18650 battery pack (7,4 Volts)
