# Fritzing sketch H-Brug (saved by Fritzing 1.0.1rc)
circuit board: 12.6858cm x 6.00755cm

parts:
  DRV8833 = Adafruit DRV8833 DC/Stepper Motor Driver [part_number="Adafruit #3297"]
  M2 = DC Motor [voltage_(max)=12V voltage_(min)=3V]
  M3 = DC Motor [voltage_(max)=12V voltage_(min)=3V]
  MH-ET_LIVE_ESP32_DEVKIT1 = MH-ET LIVE ESP32 DEVKIT 38 pins

nets:
  N1: DRV8833.AOUT2, M2.pin_2
  N2: DRV8833.AOUT1, M2.pin_1
  N3: DRV8833.BOUT1, M3.pin_1
  N4: DRV8833.BOUT2, M3.pin_2
  N5: DRV8833.VMOTOR, MH-ET_LIVE_ESP32_DEVKIT1.5V
  GND: DRV8833.GND, MH-ET_LIVE_ESP32_DEVKIT1.GND
  N6: DRV8833.BIN1, MH-ET_LIVE_ESP32_DEVKIT1.IO12
  N7: DRV8833.BIN2, MH-ET_LIVE_ESP32_DEVKIT1.IO14
  N8: DRV8833.AIN2, MH-ET_LIVE_ESP32_DEVKIT1.IO27
  N9: DRV8833.AIN1, MH-ET_LIVE_ESP32_DEVKIT1.IO26

custom parts:
  Adafruit DRV8833 DC/Stepper Motor Driver: Spin two DC motors or step one bi-polar or uni-polar stepper with up to 1.2A per channel using the DRV8833. This motor driver chip is a nice alternative to the TB6612 driver. Like that chip, you get 2 full H-bridges, but this chip is better for low voltage uses (can run from 2.7V up to 10.8V motor power) and has built in current limiting capability. We set it up for 1A current limiting so you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
  MH-ET LIVE ESP32 DEVKIT 38 pins: http://mh.nodebb.com/topic/2/mh-et-live-esp32-devkit
