# Fritzing sketch Interrupt (saved by Fritzing 1.0.1rc)
breadboards: 1

parts:
  MH-ET_LIVE_ESP32_DEVKIT1 = MH-ET LIVE ESP32 DEVKIT 38 pins
  LED1 = LEDs [package=led10mm]
  S1 = Momentary Switch [package=ksa_sealed_tac_switch]
  R1 = Resistor [tolerance=±5% power=0.25W resistance=220 package=THT]

nets:
  N1: MH-ET_LIVE_ESP32_DEVKIT1.GND#64, S1.2, R1.Pin_1
  N2: MH-ET_LIVE_ESP32_DEVKIT1.IO17, LED1.A
  N3: MH-ET_LIVE_ESP32_DEVKIT1.IO2, S1.4
  N4: LED1.C, R1.Pin_0

custom parts:
  MH-ET LIVE ESP32 DEVKIT 38 pins: http://mh.nodebb.com/topic/2/mh-et-live-esp32-devkit
